# Fritzing sketch keyboard (saved by Fritzing 0.9.3b)
breadboards: 1

parts:
  Part1 = Photon
  J1 = Piezo Speaker
  POT1 = Breadboard Trimpot
  S4 = Pushbutton [package="[THT]"]
  S3 = Pushbutton [package="[THT]"]
  S1 = Pushbutton [package="[THT]"]
  R4 = Resistor [tolerance=±5% resistance=10k package="2512 [SMD]"]
  R5 = Resistor [tolerance=±5% resistance=10k package="2512 [SMD]"]
  R6 = Resistor [tolerance=±5% resistance=10k package="2512 [SMD]"]

nets:
  N1: Part1.GND, J1.pin1, POT1.PIN3, S4.Pin_1, S4.Pin_2, S3.Pin_1, S3.Pin_2, S1.Pin_1, S1.Pin_2
  N2: Part1.D0, POT1.PIN1
  N3: Part1.D1, S1.Pin_3, S1.Pin_4, R4.Pin_1
  N4: Part1.D2, S3.Pin_3, S3.Pin_4, R5.Pin_1
  N5: Part1.D3, S4.Pin_3, S4.Pin_4, R6.Pin_1
  N6: Part1.3V3, R4.Pin_0, R5.Pin_0, R6.Pin_0
  N7: J1.pin2, POT1.PIN2
