# Fritzing sketch sequencer (saved by Fritzing 0.9.3b)
breadboards: 1

parts:
  Part1 = Photon
  LED1 = LED - 5mm [color="Red (633nm)" package="5 mm [THT]"]
  R1 = Resistor [tolerance=±5% resistance=220 package=THT]
  LED2 = LED - 5mm [color="Red (633nm)" package="5 mm [THT]"]
  R2 = Resistor [tolerance=±5% resistance=220 package=THT]
  LED3 = LED - 5mm [color="Red (633nm)" package="5 mm [THT]"]
  R3 = Resistor [tolerance=±5% resistance=220 package=THT]
  LED4 = LED - 5mm [color="Red (633nm)" package="5 mm [THT]"]
  R4 = Resistor [tolerance=±5% resistance=220 package=THT]
  S1 = Pushbutton [package="[THT]"]
  S2 = Pushbutton [package="[THT]"]
  S3 = Pushbutton [package="[THT]"]
  S4 = Pushbutton [package="[THT]"]
  R5 = Resistor [tolerance=±5% resistance=10k package=THT]
  R6 = Resistor [tolerance=±5% resistance=10k package=THT]
  R7 = Resistor [tolerance=±5% resistance=10k package=THT]
  R8 = Resistor [tolerance=±5% resistance=10k package=THT]
  POT1 = Breadboard Trimpot
  J1 = Piezo Speaker

nets:
  N1: Part1.A0, S2.Pin_1, S2.Pin_2, R7.Pin_0
  N2: Part1.A1, S1.Pin_1, S1.Pin_2, R5.Pin_0
  N3: Part1.A2, S3.Pin_1, S3.Pin_2, R6.Pin_0
  N4: Part1.A3, S4.Pin_1, S4.Pin_2, R8.Pin_0
  N5: Part1.A5, POT1.PIN1
  N6: Part1.GND, R1.Pin_1, R2.Pin_1, R3.Pin_1, R4.Pin_1, R5.Pin_1, R6.Pin_1, R7.Pin_1, R8.Pin_1, POT1.PIN3, J1.pin1
  N7: Part1.D0, LED1.cathode
  N8: Part1.D1, LED2.cathode
  N9: Part1.D2, LED3.cathode
  N10: Part1.D3, LED4.cathode
  N11: Part1.3V3, S1.Pin_3, S1.Pin_4, S2.Pin_3, S2.Pin_4, S3.Pin_3, S3.Pin_4, S4.Pin_3, S4.Pin_4
  N12: LED1.anode, R1.Pin_0
  N13: LED2.anode, R2.Pin_0
  N14: LED3.anode, R3.Pin_0
  N15: LED4.anode, R4.Pin_0
  N16: POT1.PIN2, J1.pin2
