# Fritzing sketch resistors (saved by Fritzing 0.9.3b)
breadboards: 1

parts:
  Part1 = Photon
  R1 = Temperature Sensor (Thermistor) [thermistor_type=NTC package=THT]
  R2 = PHOTOCELL [package=photocell-kit]
  R3 = Resistor [tolerance=±5% resistance=10k package="0402 [SMD]"]
  R4 = Resistor [tolerance=±5% resistance=10k package="0402 [SMD]"]
  R5 = Resistor [tolerance=±5% resistance=10k package="0402 [SMD]"]
  POT1 = Breadboard Trimpot
  SparkFun1 = SoftPot Membrane Potentiometer - 50mm [part_number=SEN-08680]
  LED1 = RGB LED (com. cathode, rgb) [package="5 mm [THT]"]
  R6 = Resistor [tolerance=±5% resistance=220 package="0805 [SMD]"]
  R7 = Resistor [tolerance=±5% resistance=220 package="0805 [SMD]"]
  R8 = Resistor [tolerance=±5% resistance=220 package="0805 [SMD]"]

nets:
  N1: Part1.A1, Part1.3V3, R1.pin_0, R2.P$1, R5.Pin_0, POT1.PIN1, SparkFun1.leg1
  N2: Part1.A2, R1.pin_1, R3.Pin_0
  N3: Part1.A3, R2.P$2, R4.Pin_0
  N4: Part1.A4, POT1.PIN2
  N5: Part1.A5, SparkFun1.wiper
  N6: Part1.GND, R3.Pin_1, R4.Pin_1, R5.Pin_1, POT1.PIN3, SparkFun1.leg2, LED1.common_cathode
  N7: Part1.D0, R6.Pin_1
  N8: Part1.D1, R7.Pin_1
  N9: Part1.D2, R8.Pin_1
  N10: LED1.red_anode, R6.Pin_0
  N11: LED1.green_anode, R7.Pin_0
  N12: LED1.blue_anode, R8.Pin_0

custom parts:
  SoftPot Membrane Potentiometer - 50mm: These are very thin variable potentiometers. By pressing down on various parts of the strip, the resistance linearly changes from 100Ohms to 10,000Ohms allowing the user to very accurately calculate the relative position on the strip. Can be used as an accurate positional indicator for CNC head positioning, variable user input (volume level input for example), straight user input (multiple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
