# Fritzing sketch tone_generator (saved by Fritzing 0.9.3b)
breadboards: 1

parts:
  Part1 = Photon
  POT1 = Breadboard Trimpot
  POT2 = Breadboard Trimpot
  POT3 = Breadboard Trimpot
  POT4 = Breadboard Trimpot
  TRS1 = Audio Jack (TRS) 3.5mm [package="PG203J [THT]"]
  POT5 = Breadboard Trimpot

nets:
  N1: Part1.A0, POT1.PIN2
  N2: Part1.A1, POT2.PIN2
  N3: Part1.A2, POT3.PIN2
  N4: Part1.A3, POT4.PIN2
  N5: Part1.GND, POT1.PIN3, POT2.PIN3, POT3.PIN3, POT4.PIN3, TRS1.Sleeve, POT5.PIN3
  N6: Part1.D1, POT5.PIN1
  N7: Part1.3V3, POT1.PIN1, POT2.PIN1, POT3.PIN1, POT4.PIN1
  N8: TRS1.Ring, TRS1.Tip, POT5.PIN2
