# Fritzing sketch sampler (saved by Fritzing 0.9.3b)
breadboards: 1

parts:
  Part1 = Photon
  TRS1 = Audio Jack (TRS) 3.5mm [package="4Ucon 08780 [THT]"]
  Part2 = Adafruit MPR121

nets:
  GND: Part1.GND, TRS1.Sleeve, Part2.GND
  N1: Part1.D0, Part2.SDA
  N2: Part1.D1, Part2.SCL
  N3: Part1.D2, TRS1.Tip
  3V3: Part1.3V3, Part2.VIN

custom parts:
  Adafruit MPR121: Add lots of touch sensors to your next microcontroller project with this easy-to-use 12-channel capacitive touch sensor breakout board, starring the MPR121. This chip can handle up to 12 individual touch pads. The MPR121 has support for only I2C, which can be implemented with nearly any microcontroller. You can select one of 4 addresses with the ADDR pin, for a total of 48 capacitive touch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
