# Fritzing sketch spi (saved by Fritzing 0.9.3b)
breadboards: 1

parts:
  Part1 = Adafruit MicroSD card breakout board [part_number="Adafruit #254"]
  Part2 = Photon
  TRS1 = Audio Jack (TRS) 3.5mm [package="4Ucon 08780 [THT]"]

nets:
  +3V3: Part1.+3V3, Part2.3V3
  GND: Part1.GND, Part2.GND, TRS1.Sleeve
  N1: Part1.CLK, Part2.A5
  N2: Part1.DO, Part2.A4
  N3: Part1.DI, Part2.A3
  N4: Part1.CS, Part2.A2
  N5: Part2.DAC, TRS1.Ring

custom parts:
  Adafruit MicroSD card breakout board: Not just a simple breakout board, this microSD adapter goes the extra mile - designed for ease of use. Onboard 5v->3v regulator provides 150mA for power-hungry cards 3v level shifting means you can use this with ease on either 3v or 5v systems Uses a proper level shifting chip, not resistors: less problems, and faster read/write access Use 3 or 4 digital pins to read and write 2Gb+ of storage!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
