# Fritzing sketch playbackcapture (saved by Fritzing 0.9.3b)
breadboards: 1

parts:
  Part1 = Adafruit MicroSD card breakout board [part_number="Adafruit #254"]
  Part2 = Photon
  TRS1 = Audio Jack (TRS) 3.5mm [package="4Ucon 08780 [THT]"]
  Part3 = Adafruit MAX9814 Electret Microphone Amplifier [part_number="Adafruit #1713"]
  S1 = Pushbutton [package="[SMD]"]
  R1 = Resistor [tolerance=±5% resistance=10k package=THT]

nets:
  +3V3: Part1.+3V3, Part2.3V3, Part3.VDD, Part3.GAIN, S1.Pin_3, S1.Pin_4
  GND: Part1.GND, Part2.GND, TRS1.Sleeve, Part3.GND, R1.Pin_1
  N1: Part1.CLK, Part2.A3
  N2: Part1.DO, Part2.A4
  N3: Part1.DI, Part2.A5
  N4: Part1.CS, Part2.A2
  N5: Part2.A0, Part3.OUTPUT
  N6: Part2.DAC, TRS1.Ring
  N7: Part2.D0, S1.Pin_1, S1.Pin_2, R1.Pin_0

custom parts:
  Adafruit MicroSD card breakout board: Not just a simple breakout board, this microSD adapter goes the extra mile - designed for ease of use. Onboard 5v->3v regulator provides 150mA for power-hungry cards 3v level shifting means you can use this with ease on either 3v or 5v systems Uses a proper level shifting chip, not resistors: less problems, and faster read/write access Use 3 or 4 digital pins to read and write 2Gb+ of storage!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
  Adafruit MAX9814 Electret Microphone Amplifier: Add an ear to your project with this well-designed electret microphone amplifier with AGC. This fully assembled and tested board comes with a 20-20KHz electret microphone soldered on. For the amplification, we use the Maxim MAX9814, a specialty chip that is designed for amplifying electret microphones in situations where the loudness of the audio isn't predictable. This fancy microphone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
