# Fritzing sketch i2c (saved by Fritzing 0.9.3b)
breadboards: 1

parts:
  Part2 = Photon
  LED1 = RGB LED (com. cathode, rbg) [package="5 mm [THT]"]
  R1 = Resistor [tolerance=±5% resistance=220 package="0805 [SMD]"]
  R2 = Resistor [tolerance=±5% resistance=220 package="0805 [SMD]"]
  R3 = Resistor [tolerance=±5% resistance=220 package="0805 [SMD]"]
  Part6 = IMU Digital Combo Board 6DOF
  Part4 = Color Sensor Breakout ADJD-S311  # not connected

nets:
  N1: Part2.A4, R1.Pin_1
  N2: Part2.A5, R3.Pin_1
  GND: Part2.GND, Part6.GND
  N3: Part2.D2, R2.Pin_1
  3V3: Part2.3V3, Part6.3.3V
  N4: LED1.blue_anode, R1.Pin_0
  N5: LED1.green_anode, R3.Pin_0

notes:
  Neither the Sparkfun ISL29125 nor the MPU-6050 have Fritzing parts. These are close relatives. Each have the same four i2c connections: GND, VCC, SDA, SCL
  SDA->D0 and SCL->D1
