# Fritzing sketch solenoid (saved by Fritzing 0.9.3b)
breadboards: 1

parts:
  Part2 = Photon
  L1 = Solenoid
  D1 = Zener Diode [part_number=1N4732A breakdown_voltage=3.6V package="Melf DO-213 AB [SMD]"]
  VCC1 = Battery
  Q1 = TIP120 Hi-Current Darlington Transistor
  R1 = Resistor [tolerance=±5% resistance=220 package="2010 [SMD]"]
  U1 = TMP36 [package=to-92-kit]

nets:
  N1: Part2.A0, U1.VOUT
  GND: Part2.GND, VCC1.-, Q1.EMITTER, U1.GND
  N2: Part2.D1, R1.Pin_0
  3V3: Part2.3V3, U1.VCC
  N3: L1.pin1, D1.anode, Q1.COLLECTOR
  N4: L1.pin2, D1.cathode, VCC1.+
  N5: Q1.BASE, R1.Pin_1
