# Fritzing sketch amp (saved by Fritzing 0.9.3b)
breadboards: 1

parts:
  Part2 = Photon
  Part3 = Adafruit MAX98306 Stereo 3.7W Class D Audio Amplifier [part_number="Adafruit #987"]
  SPKR1 = Loudspeaker
  POT1 = Breadboard Trimpot
  SPKR2 = Loudspeaker

nets:
  N1: Part2.DAC, POT1.PIN1
  N2: Part2.GND, POT1.PIN3
  N3: Part3.LOUT-, SPKR1.pin1
  N4: Part3.LOUT+, SPKR1.pin2
  N5: Part3.ROUT+, SPKR2.pin2
  N6: Part3.ROUT-, SPKR2.pin1

custom parts:
  Adafruit MAX98306 Stereo 3.7W Class D Audio Amplifier: This incredibly small stereo amplifier is surprisingly powerful - able to deliver 2 x 3.7W channels into 3 ohm impedance speakers. Inside the miniature chip is a class D controller, able to run from 2.7V-5.5VDC. Since the amp is a class D, its incredibly efficient (over 90% efficient when driving an 8Ω speaker at over a Watt) - making it perfect for portable and battery-powered projects. It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
